# Fritzing sketch Untitled Sketch (saved by Fritzing 0.9.3b)
breadboards: 1

parts:
  R1 = Resistor [tolerance=±5% resistance=220 package=THT]
  R2 = Resistor [tolerance=±5% resistance=220 package=THT]
  R3 = Resistor [tolerance=±5% resistance=220 package=THT]
  R4 = Resistor [tolerance=±5% resistance=220 package=THT]
  C1 = Ceramic Capacitor [capacitance=100nF package="100 mil [THT, multilayer]"]
  C2 = Ceramic Capacitor [capacitance=100nF package="100 mil [THT, multilayer]"]
  Q1 = NPN-Transistor [package="TO92 [THT]"]
  Q2 = NPN-Transistor [package="TO92 [THT]"]

nets:
  5V: R1.Pin_0, R2.Pin_0, R3.Pin_0, R4.Pin_0
  N1: R1.Pin_1, C1.0, Q1.C
  N2: R2.Pin_1, C1.1, Q2.B
  N3: R3.Pin_1, C2.0, Q1.B
  N4: R4.Pin_1, C2.1, Q2.C
  GND: Q1.E, Q2.E
